# Fritzing sketch Solar_LED_Circuit_Sketch_Full (saved by Fritzing 0.9.5d)

parts:
  Part1 = TPS63020 power supply module
  M1 = DOIT Esp32 DevKit v1 (30 pins long, 11 pins width) [part_number=ESP32S-PIN30]
  R3 = Resistor [tolerance=±5% resistance=220 package="0402 [SMD]"]
  M2 = RioRand LM2596
  VCC1 = 4 x AAA Battery Mount
  J2 = screw terminal, 6 pins
  Part2 = Solar Panel [package="Renogy 50 Watts 12 Volt Monocrystalline Bendable Solar Panel"]
  D1 = Zener Diode [part_number=1N4732A breakdown_voltage=3.6V package="300 mil [THT]"]
  A2 = circuit breaker C120N-1P
  INA1 = INA219 DC Current Sensor Breakout
  Q1 = Basic FET N-Channel [package="D2Pak [SMD]"]
  LED1 = White LED - Rect 5x2x7mm [package="5x2x7 mm [THT]"]  # not connected
  R6 = Resistor [tolerance=±5% resistance=10k package="0402 [SMD]"]  # not connected
  DS1 = DS18B20 1-Wire Temperature Sensor Probe Cable
  F1 = Fan - Ventilador [package=THT]
  Q2 = Basic FET N-Channel [package="D2Pak [SMD]"]
  R7 = Resistor [tolerance=±5% resistance=220 package="0402 [SMD]"]  # not connected
  R8 = Resistor [tolerance=±5% resistance=10k package="0402 [SMD]"]  # not connected
  D5 = Zener Diode [part_number=1N4732A breakdown_voltage=3.6V package="300 mil [THT]"]  # not connected
  DS3 = DS18B20 1-Wire Temperature Sensor Probe Cable
  R9 = Resistor [tolerance=±5% resistance=4.7 package="0402 [SMD]"]
  ZS-042_RTC1 = ZS-042 RTC Module
  J3 = screw terminal, 6 pins

nets:
  N1: Part1.GND_P1_1, Part1.PS, Q1.source, DS1.GND, Q2.source
  GND: Part1.GND_P2_1, M1.GND, INA1.GND, ZS-042_RTC1.GND
  N2: Part1.VOUT_2, J3.pin1
  N3: M1.3V3, J2.pin6
  N4: M1.D4, DS1.shield
  N5: M1.D18, R3.Pin_1
  N6: M1.D21, INA1.SDA, ZS-042_RTC1.SDA
  N7: M1.D22, INA1.SCL, ZS-042_RTC1.SCL
  N8: M2.Pin_1, J2.pin1, Part2.Connector_1, D1.cathode, D1.anode
  N9: M2.Pin_2, J2.pin2, Part2.Connector_2
  N10: M2.Pin_3, VCC1.+, A2.Pin_2
  N11: M2.Pin_4, VCC1.-, J2.pin4
  N12: J2.pin5, A2.Pin_1
  VDD: DS1.VDD, DS3.VDD, R9.Pin_1
  N13: F1.GND, Q2.drain
  N14: DS3.shield, R9.Pin_0

notes:
  CC/CV Buck Coverter
  20A 300W
  Solar Panel Mono 18V 50W
  Battery
  32140 x 4 = 60A
  (Included BMS)
  Diode 10SQ050
  Terminal Block TB1506
  DC Breaker
  1P 16A
  Line/Input
  Load/Output
  INA226 Module
  ESP32
  R220 Ohm (P1-Gate)
  622 LED
  3.2v 300W
  LED Cathode (P2-Drain)
  R10 kOhm
  (P3-Source+P1-Gate)
  TPS63020
  5v
  VBus Line
  5v Fan
  R4.7 kOhm
  DS18B20
  Temp Sensor
  DS3231
  Clock Module
  Terminal Block 1 = Solar +
  2 = Solar -
  3 = Batt +
  4 = Com GND
  5 = Load Solar or Batt
  6 = 3.3v Source (Green)
  7 = 5v Source (Purple)

custom parts:
  TPS63020 power supply module: TPS63020 is a power supply module (buck-boost) with a efficiency as high as 96%. Input voltage range is from 1.8V to 5.5V. Output voltage is set via R1 and R3, most modules have a output voltage of 5V configured as default. This corresponds to R1=110K and R3=1M. For a output voltage of 3.3V R1 has to be changed to 180K (R3 can be kept at 1M). The output current is up to 3A. Switches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
  DOIT Esp32 DevKit v1 (30 pins long, 11 pins width): The DOIT Esp32 DevKit v1 is one of the development board created by DOIT to evaluate the ESP-WROOM-32 module. It is based on the ESP32 microcontroller that boasts Wifi, Bluetooth, Ethernet and Low Power support all in a single chip. (vanepp) made breadboard work, adjusted pin numbering and labels and reduced size of schematic and cleaned up pcb. This chip is 30pins long (2 x15) and 11 pins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
  Solar Panel: Renogy 50 Watts 12 Volt Solar Panel
  circuit breaker C120N-1P: C120N - circuit breaker - 1P - 125A - C curve.
  INA219 DC Current Sensor Breakout: INA DC Current Sensor Breakout
  White LED - Rect 5x2x7mm: A generic rectangular white LED (~1.8V) 5mm x 2mm x 7mm
  Fan - Ventilador: Ventilador de 2 pines, se encuentra comunmente en computadoras de escritorio
