# Fritzing sketch Solar_LED_Circuit_Sketch_No_Controller (saved by Fritzing 0.9.5d)

parts:
  M2 = RioRand LM2596
  VCC1 = 4 x AAA Battery Mount
  J2 = screw terminal, 6 pins
  Part2 = Solar Panel [package="Renogy 50 Watts 12 Volt Monocrystalline Bendable Solar Panel"]
  D1 = Zener Diode [part_number=1N4732A breakdown_voltage=3.6V package="300 mil [THT]"]
  A2 = circuit breaker C120N-1P
  LED1 = White LED - Rect 5x2x7mm [package="5x2x7 mm [THT]"]  # not connected

nets:
  N1: M2.Pin_1, J2.pin1, Part2.Connector_1, D1.cathode, D1.anode
  N2: M2.Pin_2, J2.pin2, Part2.Connector_2
  N3: M2.Pin_3, J2.pin5, A2.Pin_1
  N4: M2.Pin_4, VCC1.-, J2.pin4

notes:
  CC/CV Buck Coverter
  20A 300W
  Solar Panel Mono 18V 50W
  Battery
  32140 x 4 = 60A
  (Included BMS)
  Diode 10SQ050
  Terminal Block TB1506
  DC Breaker
  1P 16A
  622 LED
  3.2v 300W
  LED Cathode (P2-Drain)
  LED P+
  LED P-

custom parts:
  Solar Panel: Renogy 50 Watts 12 Volt Solar Panel
  circuit breaker C120N-1P: C120N - circuit breaker - 1P - 125A - C curve.
  White LED - Rect 5x2x7mm: A generic rectangular white LED (~1.8V) 5mm x 2mm x 7mm
